# Fritzing sketch Secuencia led (saved by Fritzing 0.9.3b)
breadboards: 2

parts:
  CD4017 = IC, DIP package, 16 pins [chip_label=CD4017]
  555 = IC, DIP package, 8 pins [chip_label=555]
  R1 = Resistor [tolerance=±5% resistance=1k package=THT]
  C1 = Electrolytic Capacitor [capacitance=10µF package="100 mil [THT, electrolytic]"]
  R2 = Rotary Potentiometer (Small) [maximum_resistance=10kΩ package=THT]
  R3 = Resistor [tolerance=±5% resistance=1k package=THT]
  LED1 = LED - 5mm [color="Red (633nm)" package="5 mm [THT]"]
  LED6 = LED - 5mm [color="Red (633nm)" package="5 mm [THT]"]
  LED7 = LED - 5mm [color="Red (633nm)" package="5 mm [THT]"]
  LED8 = LED - 5mm [color="Red (633nm)" package="5 mm [THT]"]
  LED9 = LED - 5mm [color="Red (633nm)" package="5 mm [THT]"]
  LED10 = LED - 5mm [color="Red (633nm)" package="5 mm [THT]"]
  LED11 = LED - 5mm [color="Red (633nm)" package="5 mm [THT]"]
  LED12 = LED - 5mm [color="Red (633nm)" package="5 mm [THT]"]
  LED13 = LED - 5mm [color="Red (633nm)" package="5 mm [THT]"]
  LED14 = LED - 5mm [color="Red (633nm)" package="5 mm [THT]"]
  LED15 = LED - 5mm [color="Red (633nm)" package="5 mm [THT]"]
  R13 = Resistor [tolerance=±5% resistance=1k package=THT]
  R12 = Resistor [tolerance=±5% resistance=1k package=THT]
  R11 = Resistor [tolerance=±5% resistance=1k package=THT]
  R10 = Resistor [tolerance=±5% resistance=1k package=THT]
  R9 = Resistor [tolerance=±5% resistance=1k package=THT]
  R8 = Resistor [tolerance=±5% resistance=1k package=THT]
  R7 = Resistor [tolerance=±5% resistance=1k package=THT]
  R6 = Resistor [tolerance=±5% resistance=1k package=THT]
  R5 = Resistor [tolerance=±5% resistance=1k package=THT]
  R4 = Resistor [tolerance=±5% resistance=1k package=THT]

nets:
  N1: CD4017.pin1, LED8.anode
  N2: CD4017.pin2, LED9.anode
  N3: CD4017.pin3, LED11.anode
  N4: CD4017.pin4, LED10.anode
  N5: CD4017.pin5, LED15.anode
  N6: CD4017.pin6, LED14.anode
  N7: CD4017.pin7, LED6.anode
  N8: CD4017.pin8, 555.pin1, C1.-, R3.Pin_1, LED8.cathode, R9.Pin_0, R9.Pin_1, R8.Pin_0, R7.Pin_0, R6.Pin_0, R5.Pin_0, R4.Pin_0
  N9: CD4017.pin9, LED12.anode
  N10: CD4017.pin10, LED7.anode
  N11: CD4017.pin11, LED13.anode
  N12: CD4017.pin13, CD4017.pin15, R13.Pin_1, R12.Pin_1, R11.Pin_1, R10.Pin_1
  N13: CD4017.pin14, 555.pin3, LED1.anode
  N14: CD4017.pin16, 555.pin4, 555.pin8, R1.Pin_0
  N15: 555.pin2, 555.pin6, C1.+, R2.wiper
  N16: 555.pin7, R1.Pin_1, R2.leg1
  N17: R3.Pin_0, LED1.cathode
  N18: LED6.cathode, R7.Pin_1
  N19: LED7.cathode, R8.Pin_1
  N20: LED9.cathode, R5.Pin_1
  N21: LED10.cathode, R6.Pin_1
  N22: LED11.cathode, R4.Pin_1
  N23: LED12.cathode, R12.Pin_0
  N24: LED13.cathode, R13.Pin_0
  N25: LED14.cathode, R11.Pin_0
  N26: LED15.cathode, R10.Pin_0

notes:
  No son necesarios los 10 resistores ni los 10 leds. En los resistores, basta con colocar solo uno común para todos.
